# Fritzing sketch layout (saved by Fritzing 0.9.0b)
breadboards: 1

parts:
  Onderdeel1 = Arduino Uno (Rev3)
  LED1 = LED - 5mm [color="Red (633nm)" package="5 mm [THT]"]
  LED2 = LED - 5mm [color="Red (633nm)" package="5 mm [THT]"]
  LED3 = LED - 5mm [color="Red (633nm)" package="5 mm [THT]"]
  LED4 = LED - 5mm [color="Red (633nm)" package="5 mm [THT]"]
  LED5 = LED - 5mm [color="Red (633nm)" package="5 mm [THT]"]
  LED6 = LED - 5mm [color="Red (633nm)" package="5 mm [THT]"]
  LED7 = LED - 5mm [color="Red (633nm)" package="5 mm [THT]"]
  LED8 = LED - 5mm [color="Red (633nm)" package="5 mm [THT]"]
  R1 = Resistor [tolerance=±5% resistance=220 package=THT]
  R2 = Resistor [tolerance=±5% resistance=220 package=THT]
  R3 = Resistor [tolerance=±5% resistance=220 package=THT]
  R4 = Resistor [tolerance=±5% resistance=220 package=THT]
  R5 = Resistor [tolerance=±5% resistance=220 package=THT]
  R6 = Resistor [tolerance=±5% resistance=220 package=THT]
  R7 = Resistor [tolerance=±5% resistance=220 package=THT]
  R8 = Resistor [tolerance=±5% resistance=220 package=THT]

nets:
  N1: Onderdeel1.D8, LED2.anode
  N2: Onderdeel1.D9_PWM, LED1.anode
  N3: Onderdeel1.D2, LED8.anode
  N4: Onderdeel1.D3_PWM, LED7.anode
  N5: Onderdeel1.D4, LED6.anode
  N6: Onderdeel1.D5_PWM, LED5.anode
  N7: Onderdeel1.D6_PWM, LED4.anode
  N8: Onderdeel1.D7, LED3.anode
  N9: Onderdeel1.GND, R1.Pin_0, R2.Pin_0, R3.Pin_0, R4.Pin_0, R5.Pin_0, R6.Pin_0, R7.Pin_0, R8.Pin_0
  N10: LED1.cathode, R1.Pin_1
  N11: LED2.cathode, R2.Pin_1
  N12: LED3.cathode, R3.Pin_1
  N13: LED4.cathode, R4.Pin_1
  N14: LED5.cathode, R8.Pin_1
  N15: LED6.cathode, R7.Pin_1
  N16: LED7.cathode, R6.Pin_1
  N17: LED8.cathode, R5.Pin_1
